# Fritzing sketch main (saved by Fritzing 0.9.4)

parts:
  MicroSD_Badusb1 = MicroSD_Badusb
  SparkFun_74HC4051_8-Channel_Mux_Breakout1 = SparkFun-74HC4051-8-Channel-Mux-Breakout [part_number=BOB-13906]

nets:
  N1: MicroSD_Badusb1.5_VCC, MicroSD_Badusb1.10_VCC, SparkFun_74HC4051_8-Channel_Mux_Breakout1.VCC
  N2: MicroSD_Badusb1.11_GND, SparkFun_74HC4051_8-Channel_Mux_Breakout1.GND

custom parts:
  MicroSD_Badusb: CJMCU 32U4TF Arduino Leonardo This virtual keyboard integrates the keyboard and USB function, which you can use it as a USB or keyboard. The main chip of this virtual keyboard is ATMEGA32U4, it can provide a USB 2.0 Full-speed. Due to its low power consumption, high performance, this module has good working performance. There is a virtual keyboard program inside this module, you can use the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
